# Fritzing sketch Tetris (saved by Fritzing 0.9.5d)
breadboards: 1

parts:
  RTR = Resistor [tolerance=±5% resistance=1k package=THT]
  RTL = Resistor [tolerance=±5% resistance=1k package=THT]
  RML = Resistor [tolerance=±5% resistance=1k package=THT]
  RDown = Resistor [tolerance=±5% resistance=1k package=THT]
  RMR = Resistor [tolerance=±5% resistance=1k package=THT]
  TurnRight = Pushbutton [package="[THT]"]
  MoveLeft = Pushbutton [package="[THT]"]
  TurnLeft = Pushbutton [package="[THT]"]
  Down = Pushbutton [package="[THT]"]
  Drop = Pushbutton [package="[THT]"]
  MoveRight = Pushbutton [package="[THT]"]
  RDrop = Resistor [tolerance=±5% resistance=1k package=THT]
  Bauteil1 = Arduino Uno (Rev3)

nets:
  N1: RTR.Pin_0, TurnRight.Pin_1, TurnRight.Pin_2, Bauteil1.D2
  GND: RTR.Pin_1, RTL.Pin_1, RML.Pin_1, RDown.Pin_1, RMR.Pin_1, RDrop.Pin_1, Bauteil1.GND
  N2: RTL.Pin_0, TurnLeft.Pin_1, TurnLeft.Pin_2, Bauteil1.D7
  N3: RML.Pin_0, MoveLeft.Pin_1, MoveLeft.Pin_2, Bauteil1.D6_PWM
  N4: RDown.Pin_0, Down.Pin_1, Down.Pin_2, Bauteil1.D5_PWM
  N5: RMR.Pin_0, MoveRight.Pin_1, MoveRight.Pin_2, Bauteil1.D3_PWM
  5V: TurnRight.Pin_3, TurnRight.Pin_4, MoveLeft.Pin_3, MoveLeft.Pin_4, TurnLeft.Pin_3, TurnLeft.Pin_4, Down.Pin_3, Down.Pin_4, Drop.Pin_3, Drop.Pin_4, MoveRight.Pin_3, MoveRight.Pin_4, Bauteil1.5V
  N6: Drop.Pin_1, Drop.Pin_2, RDrop.Pin_0, Bauteil1.D4

notes:
  Resistors: 1 KΩ
  Buttons:
  TurnLeft MoveLeft Down Drop MoveRight TurnRight
  Arduino Tetris, Beschreibung des Button Layouts auf dem Arduino.
