# Fritzing sketch Tetris (saved by Fritzing 0.9.5d)
breadboards: 1

parts:
  Bauteil1 = Arduino Uno (Rev3)
  Move_Right = Pushbutton [package="[THT]"]
  Turn_Right = Pushbutton [package="[THT]"]
  Down = Pushbutton [package="[THT]"]
  Drop = Pushbutton [package="[THT]"]
  Turn_Left = Pushbutton [package="[THT]"]
  Move_Left = Pushbutton [package="[THT]"]
  R1 = Resistor [tolerance=±5% resistance=1k package=THT]
  R2 = Resistor [tolerance=±5% resistance=1k package=THT]
  R3 = Resistor [tolerance=±5% resistance=1k package=THT]
  R4 = Resistor [tolerance=±5% resistance=1k package=THT]
  R5 = Resistor [tolerance=±5% resistance=1k package=THT]
  R6 = Resistor [tolerance=±5% resistance=1k package=THT]

nets:
  N1: Bauteil1.D2, Move_Right.Pin_1, Move_Right.Pin_2, R1.Pin_1
  N2: Bauteil1.D3_PWM, Turn_Right.Pin_1, Turn_Right.Pin_2, R2.Pin_1
  N3: Bauteil1.D4, Down.Pin_1, Down.Pin_2, R3.Pin_1
  N4: Bauteil1.D5_PWM, Drop.Pin_1, Drop.Pin_2, R4.Pin_1
  N5: Bauteil1.D6_PWM, Turn_Left.Pin_1, Turn_Left.Pin_2, R5.Pin_1
  N6: Bauteil1.D7, Move_Left.Pin_1, Move_Left.Pin_2, R6.Pin_1
  N7: Bauteil1.5V, Move_Right.Pin_3, Move_Right.Pin_4, Turn_Right.Pin_3, Turn_Right.Pin_4, Down.Pin_3, Down.Pin_4, Drop.Pin_3, Drop.Pin_4, Turn_Left.Pin_3, Turn_Left.Pin_4, Move_Left.Pin_3, Move_Left.Pin_4
  N8: Bauteil1.GND, R1.Pin_0, R2.Pin_0, R3.Pin_0, R4.Pin_0, R5.Pin_0

notes:
  Resistors: 1KΩ
  Buttons:
  7 6 5 4 3 2
  MoveLeft TurnLeft Drop Down TurnRight MoveRight

// code stored in the sketch: Tetris.ino

// #region include_dependencies
#include <Arduino.h>
#include "Arduino_LED_Matrix.h"

#define DONT_USE_CPP_STL
#define GAMESTATE_IMPLEMENTATION
#include "libraries/GameState.h"
// #endregion include_dependencies

// #region setup_globals
// #region setup_game
#define WIDTH 12
#define HEIGHT 8
GameState<HEIGHT, WIDTH> game = {};
// #endregion setup_game

ArduinoLEDMatrix matrix;
uint32_t StartTime;
bool game_over = false;
uint8_t buttons = 0;

// #region setup_buttons
int btnMoveLeftPin = 7;
int btnMoveLeftPressed;

int btnTurnLeftPin = 6;
int btnTurnLeftPressed;

int btnDropPin = 5;
int btnDropPressed;

int btnBitDownPin = 4;
int btnBitDownPressed;

int btnTurnRightPin = 3;
int btnTurnRightPressed;

int btnMoveRightPin = 2;
int btnMoveRightPressed;

// #endregion setup_buttons
// #endregion setup_globals

uint8_t get_button_data() { 
  // reset buttons
  uint8_t button_data = 0;

  // read buttons
  btnTurnLeftPressed = digitalRead(btnTurnLeftPin);
  btnMoveLeftPressed = digitalRead(btnMoveLeftPin);
  btnDropPressed = digitalRead(btnDropPin);
  btnBitDownPressed = digitalRead(btnBitDownPin);
  btnMoveRightPressed = digitalRead(btnMoveRightPin);
  btnTurnRightPressed = digitalRead(btnTurnRightPin);

  // set buttons
  if (btnTurnLeftPressed == HIGH) {
    button_data = button_data | Button::TurnLeft;
  }
  if (btnMoveLeftPressed == HIGH) {
    &button_data | Button::Left;
  }
  if (btnDropPressed == HIGH) {
    &button_data | Button::Up;
  }
  if (btnBitDownPressed == HIGH) {
    &button_data | Button::Down;
  }
  if (btnMoveRightPressed == HIGH) {
    &button_data | Button::Right;
  }
  if (btnTurnRightPressed == HIGH) {
    &button_data | Button::TurnRight;
  }

  return button_data;
};

void setup() {
  pinMode(btnTurnLeftPin, INPUT);
  pinMode(btnMoveLeftPin, INPUT);
  pinMode(btnDropPin, INPUT);
  pinMode(btnBitDownPin, INPUT);
  pinMode(btnMoveRightPin, INPUT);
  pinMode(btnTurnRightPin, INPUT);

  Serial.begin(115200);
  matrix.begin();
  StartTime = millis();
}

void loop() {
  buttons = get_button_data();
  if(!game_over && TimePeriodIsOver(StartTime, 750)){
    Serial.print("buttons: ");
    Serial.println(buttons);
    game_over = game.tick(buttons);
    matrix.loadPixels(&(game.get_curr_field()[0]), WIDTH * HEIGHT);
    if (game_over) {
      // game = &GameState<HEIGHT, WIDTH>();
    }
  }
  delay(50);
}

/** easy to use helper-function for non-blocking timing
 * @param startOfPeriod - starttime in ms
 * @param TimePersiod - time in ms
 */ 
boolean TimePeriodIsOver (uint32_t &startOfPeriod, uint32_t TimePeriod) {
  uint32_t currentMillis  = millis();
  if ( currentMillis - startOfPeriod >= TimePeriod ) {
    // more time than TimePeriod has elapsed since last time if-condition was true
    startOfPeriod = currentMillis; // a new period starts right here so set new starttime
    return true;
  }
  else return false;            // actual TimePeriod is NOT yet over
}
